# Fritzing sketch hru-com-esp32 (saved by Fritzing 1.0.1rc)
circuit board: 6.52731cm x 5.62593cm
breadboards: 1

parts:
  Q1 = MOSFET-NCHANNEL [package=sot323]
  Q2 = MOSFET-NCHANNEL [package=sot323]
  R1 = Resistor [tolerance=±5% resistance=10k package="0603 [SMD]"]
  R2 = Resistor [tolerance=±5% resistance=10k package="0603 [SMD]"]
  J1 = female pin header, 4 pins [form="♀ (female)"]
  J3 = female pin header, 5 pins [form="♀ (female)"]
  U1 = ESP-WROOM-32 [ESP-32S] Module [part_number=ESP-WROOM-32]
  J2 = female pin header, 3 pins [form="♀ (female)"]
  M1 = LM2596
  R3 = Resistor [tolerance=±5% resistance=10k package="0603 [SMD]"]

nets:
  3.3V: Q1.G, Q2.G, R1.Pin_1, R2.Pin_1, J3.pin1, U1.3V3, J2.pin3, M1.Pin_3, R3.Pin_0
  N1: Q1.S, R1.Pin_0, U1.IO27, U1.IO14, U1.IO13
  N2: Q1.D, J1.pin4
  N3: Q2.S, R2.Pin_0, U1.IO33, U1.IO25, U1.IO26
  N4: Q2.D, J1.pin3
  N5: J1.pin1, M1.Pin_1
  GND: J1.pin2, J3.pin4, U1.GND#0, U1.GND#51, J2.pin1, M1.Pin_2, M1.Pin_4
  N6: J3.pin2, U1.TXD0
  N7: J3.pin3, U1.RXD0
  N8: J3.pin5, U1.IO0
  N9: U1.EN, R3.Pin_1
  N10: U1.IO15, J2.pin2

notes:
  +15V
  ITHO port
  Gnd
  I2C SCL
  I2C SDA
  Prog port
  DHT22
  +3.3V
  TXD
  RXD
  GND
  PROG
  SDA

custom parts:
  ESP-WROOM-32 [ESP-32S] Module: Espressif ESP-WROOM-32 WiFi/Bluetooth LE microcontroller module also known as the Ai-Thinker ESP-32S module with similar formfactor. The ESP32 is a microcontroller chip with WiFi and BLE capabilities. The chip is developed by Espressif and is the successor to the popular ESP8266 WiFi module.
  LM2596: Step-down DC-DC Converter (modified to correct all views by Peter Van Epp, rustyx) Corrected the pins so the part works in all views. Changed the sizes in bb and pcb to match the data sheet. PCB view had a small outline (possibly only for wires), changed it to pads in the same places as the module and added holes in the PCB silkscreen layer where the mounting holes on the module are (you need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
